// Logisim project Project.circ as structural Verilog: 5 circuits, main circuit main
module main (
);

  ROM #(.addrWidth(16), .dataWidth(20)) rom_1 ();  // open: addr, data, sel
  Main_Control main_control_1 ();  // open: in_1, REG_DST, Jump, Branch, MEM_READ, MEM_TO_REG, OP_CODE, MEM_WRITE, ALU_SOURCE, REG_WRITE
  ALU alu_1 ();  // open: in_3, LShift, A, B, out_6, in_4, out_8, out_7, out_9
  Register_File register_file_1 ();  // open: out_8, out_9, in_4, in_5, in_6, in_7, in_3, in_2, in_1
endmodule

module ALU (
  input  [19:0] A,
  input  [19:0] B,
  input  in_3,
  input  [3:0] in_4,
  input  [4:0] LShift,
  output [19:0] out_6,
  output out_7,
  output out_8,
  output out_9
);

  wire comparator_1_lt;
  wire [19:0] adder_1_out, and_1_out, bit_extender_1_out, not_1_out, or_1_out, shifter_1_out, shifter_2_out,
       subtractor_1_out, xor_1_out;

  assign and_1_out = A & B;  // AND_Gate and_1, 20 bits wide
  assign or_1_out = A | B;  // OR_Gate or_1, 20 bits wide
  assign not_1_out = ~A;  // NOT_Gate not_1, 20 bits wide
  assign xor_1_out = A ^ B;  // XOR_Gate xor_1, 20 bits wide
  Adder #(.width(20)) adder_1 (.a(A), .b(B), .out(adder_1_out), .cin(in_3), .cout(out_7));
  Subtractor #(.width(20)) subtractor_1 (.a(A), .b(B), .out(subtractor_1_out), .bin(in_3), .bout(out_9));
  assign bit_extender_1_out = {{19{1'b0}}, comparator_1_lt};  // Bit_Extender bit_extender_1
  Comparator #(.width(20)) comparator_1 (.a(A), .b(B), .eq(out_8), .lt(comparator_1_lt));  // open: gt
  Shifter #(.width(20)) shifter_1 (.in(A), .\dist (LShift), .out(shifter_1_out));
  Shifter #(.width(20), .shift("lr")) shifter_2 (.in(A), .\dist (LShift), .out(shifter_2_out));
  Multiplexer #(.select(4), .width(20)) multiplexer_1 (
    .in0({20{1'b0}}), .in1(and_1_out), .in2(or_1_out), .in3(not_1_out), .in4(xor_1_out), .in5(adder_1_out),
    .in6(subtractor_1_out), .in7(bit_extender_1_out), .in8(shifter_1_out), .in9(shifter_2_out),
    .in10({20{1'b0}}), .in11({20{1'b0}}), .in12({20{1'b0}}), .in13({20{1'b0}}), .in14({20{1'b0}}),
    .in15({20{1'b0}}), .out(out_6), .sel(in_4));  // open: en
endmodule

module Register_File (
  input  [19:0] in_1,
  input  [1:0] in_2,
  input  [1:0] in_3,
  input  [1:0] in_4,
  input  in_5,
  input  in_6,
  input  in_7,
  output [19:0] out_8,
  output [19:0] out_9
);

  wire and_1_out, and_2_out, and_3_out, and_4_out, decoder_1_out0, decoder_1_out1, decoder_1_out2,
       decoder_1_out3;
  wire [19:0] register_1_q, register_2_q, register_3_q, register_4_q;

  Decoder #(.select(2), .enable("false")) decoder_1 (
    .out0(decoder_1_out0), .out1(decoder_1_out1), .out2(decoder_1_out2), .out3(decoder_1_out3), .sel(in_4));
  and and_1 (and_1_out, decoder_1_out0, in_5);
  and and_2 (and_2_out, decoder_1_out1, in_5);
  and and_3 (and_3_out, decoder_1_out2, in_5);
  and and_4 (and_4_out, decoder_1_out3, in_5);
  Register #(.width(20)) register_1 (.D(in_1), .en(and_1_out), .Q(register_1_q), .clk(in_6), .clr(in_7));
  Register #(.width(20)) register_2 (.D(in_1), .en(and_2_out), .Q(register_2_q), .clk(in_6), .clr(in_7));
  Register #(.width(20)) register_3 (.D(in_1), .en(and_3_out), .Q(register_3_q), .clk(in_6), .clr(in_7));
  Register #(.width(20)) register_4 (.D(in_1), .en(and_4_out), .Q(register_4_q), .clk(in_6), .clr(in_7));
  Multiplexer #(.select(2), .width(20), .enable("false")) multiplexer_1 (
    .in0(register_1_q), .in1(register_2_q), .in2(register_3_q), .in3(register_4_q), .out(out_8), .sel(in_2));
  Multiplexer #(.select(2), .width(20), .enable("false")) multiplexer_2 (
    .in0(register_1_q), .in1(register_2_q), .in2(register_3_q), .in3(register_4_q), .out(out_9), .sel(in_3));

  // Notes on the sheet:
  //   write data
  //   write signal
  //   data
  //   read data 1
  //   read data 2
endmodule

module Main_Control (
  input  [3:0] in_1,
  output REG_DST,
  output Jump,
  output Branch,
  output MEM_READ,
  output MEM_TO_REG,
  output [3:0] OP_CODE,
  output MEM_WRITE,
  output ALU_SOURCE,
  output REG_WRITE
);

  wire decoder_1_out3, decoder_1_out4, decoder_1_out5, decoder_1_out6, decoder_1_out7, decoder_1_out8,
       decoder_1_out9, decoder_1_out10, decoder_1_out11, decoder_1_out12, decoder_1_out14;

  Decoder #(.select(4)) decoder_1 (
    .out1(MEM_READ), .out2(MEM_WRITE), .out3(decoder_1_out3), .out4(decoder_1_out4), .out5(decoder_1_out5),
    .out6(decoder_1_out6), .out7(decoder_1_out7), .out8(decoder_1_out8), .out9(decoder_1_out9),
    .out10(decoder_1_out10), .out11(decoder_1_out11), .out12(decoder_1_out12), .out13(Branch),
    .out14(decoder_1_out14), .out15(Jump), .sel(in_1));  // open: out0, en
  or or_1 (OP_CODE[3], decoder_1_out11, decoder_1_out12);
  or or_2 (REG_DST, decoder_1_out11, MEM_READ, decoder_1_out5, decoder_1_out6, decoder_1_out12);
  or or_3 (OP_CODE[0], MEM_READ, MEM_WRITE, decoder_1_out3, decoder_1_out5, decoder_1_out7, decoder_1_out10, decoder_1_out12, Jump);
  or or_4 (OP_CODE[1], decoder_1_out4, decoder_1_out6, decoder_1_out8, decoder_1_out10, decoder_1_out14);
  or or_5 (OP_CODE[2], MEM_READ, MEM_WRITE, decoder_1_out3, decoder_1_out4, decoder_1_out6, decoder_1_out9, decoder_1_out14, decoder_1_out5);
  or or_6 (ALU_SOURCE, MEM_READ, decoder_1_out5, MEM_WRITE, decoder_1_out6);
  or or_7 (REG_WRITE, MEM_READ, decoder_1_out5, decoder_1_out6, decoder_1_out3, decoder_1_out4, decoder_1_out7, decoder_1_out8, decoder_1_out9, decoder_1_out10, decoder_1_out11, decoder_1_out12, decoder_1_out14);

  assign MEM_TO_REG = MEM_READ;
endmodule

module Final_Datapath (
  output [3:0] opcode,
  output [1:0] rs,
  output [1:0] rt,
  output [1:0] rd,
  output out_5,
  output out_6
);

  wire alu_1_out_8, and_1_out, button_1_out, clock_1_out, main_control_1_alu_source, main_control_1_branch,
       main_control_1_jump, main_control_1_mem_read, main_control_1_mem_to_reg, main_control_1_mem_write,
       main_control_1_reg_dst, main_control_1_reg_write, not_1_out;
  wire [1:0] multiplexer_1_out;
  wire [3:0] main_control_1_op_code;
  wire [4:0] bit_extender_2_out;
  wire [15:0] adder_1_out, adder_2_out, bit_extender_3_out, bit_extender_4_out, multiplexer_3_out,
       multiplexer_4_out, register_1_q;
  wire [19:0] alu_1_out_6, bit_extender_1_out, multiplexer_2_out, multiplexer_5_out, ram_1_data,
       register_file_1_out_8, register_file_1_out_9;
  wire [19:10] rom_1_data;

  not not_1 (not_1_out, clock_1_out);
  Clock clock_1 (.out(clock_1_out));
  Register #(.width(16)) register_1 (.D(multiplexer_4_out), .Q(register_1_q), .clk(not_1_out));  // open: en, clr
  ROM #(.addrWidth(16), .dataWidth(20)) rom_1 (
    .addr(register_1_q), .data({rom_1_data, opcode, rs, rt, rd}));  // open: sel
  Adder #(.width(16)) adder_1 (.a(register_1_q), .b(16'h1), .out(adder_1_out));  // open: cin, cout
  Multiplexer #(.width(2), .enable("false")) multiplexer_1 (
    .in0(rd), .in1(rt), .out(multiplexer_1_out), .sel(main_control_1_reg_dst));
  assign bit_extender_1_out = {{18{1'b0}}, rd};  // Bit_Extender bit_extender_1
  assign bit_extender_2_out = {{3{1'b0}}, rd};  // Bit_Extender bit_extender_2
  Main_Control main_control_1 (
    .in_1(opcode), .REG_DST(main_control_1_reg_dst), .Jump(main_control_1_jump),
    .Branch(main_control_1_branch), .MEM_READ(main_control_1_mem_read),
    .MEM_TO_REG(main_control_1_mem_to_reg), .OP_CODE(main_control_1_op_code),
    .MEM_WRITE(main_control_1_mem_write), .ALU_SOURCE(main_control_1_alu_source),
    .REG_WRITE(main_control_1_reg_write));
  Button button_1 (.out(button_1_out));
  Register_File register_file_1 (
    .out_8(register_file_1_out_8), .out_9(register_file_1_out_9), .in_4(multiplexer_1_out),
    .in_5(main_control_1_reg_write), .in_6(clock_1_out), .in_7(button_1_out), .in_3(rt), .in_2(rs),
    .in_1(multiplexer_5_out));
  Bit_Extender #(.in_width(20)) bit_extender_3 (.in(bit_extender_1_out), .out(bit_extender_3_out));
  Multiplexer #(.width(20), .enable("false")) multiplexer_2 (
    .in0(register_file_1_out_9), .in1(bit_extender_1_out), .out(multiplexer_2_out),
    .sel(main_control_1_alu_source));
  Adder #(.width(16)) adder_2 (.a(adder_1_out), .b(bit_extender_3_out), .out(adder_2_out));  // open: cin, cout
  Multiplexer #(.width(16), .enable("false")) multiplexer_3 (
    .in0(adder_1_out), .in1(adder_2_out), .out(multiplexer_3_out), .sel(and_1_out));
  and and_1 (and_1_out, main_control_1_branch, alu_1_out_8);
  ALU alu_1 (
    .in_3(1'b0), .LShift(bit_extender_2_out), .A(register_file_1_out_8), .B(multiplexer_2_out),
    .out_6(alu_1_out_6), .in_4(main_control_1_op_code), .out_8(alu_1_out_8), .out_7(out_5), .out_9(out_6));
  Multiplexer #(.width(16), .enable("false")) multiplexer_4 (
    .in0(multiplexer_3_out), .in1({register_1_q[15:6], rs, rt, rd}), .out(multiplexer_4_out),
    .sel(main_control_1_jump));
  Bit_Extender #(.in_width(20)) bit_extender_4 (.in(alu_1_out_6), .out(bit_extender_4_out));
  RAM #(.addrWidth(16), .dataWidth(20), .bus("separate")) ram_1 (
    .addr(bit_extender_4_out), .din(register_file_1_out_9), .data(ram_1_data),
    .str(main_control_1_mem_write), .clk(clock_1_out), .ld(main_control_1_mem_read));  // open: sel, clr
  Multiplexer #(.width(20), .enable("false")) multiplexer_5 (
    .in0(alu_1_out_6), .in1(ram_1_data), .out(multiplexer_5_out), .sel(main_control_1_mem_to_reg));

  // Notes on the sheet:
  //   contents of rom_1 (hex, n*v repeats v):
  //   2c3 75 7a 7f c7 13f 147 197 1c4 204 244 280 36f 0 0 0 3c3 31*0 3c7
endmodule
